// Digital circuit ouex.dig as structural Verilog
module ouex (
  input  E1,
  input  E2,
  output S
);

  xor xor_1 (S, E1, E2);
endmodule

/* Test case Table de vérité:
E1 E2 S
0  0  0
1  0  1
0  1  1
1  1  0
*/
